// Logisim project cath_mind_circuit.circ as structural Verilog: 10 circuits, main circuit main
module main (
  input  Save,
  input  Save_2,
  input  Save_3,
  input  Save_4
);

  wire button_1_out, button_2_out, button_4_out, button_5_out, button_6_out, game_logic_1_turna,
       game_logic_1_turnb, game_logic_1_turnc, game_logic_1_turnd, rgb_video_1_p1, rgb_video_1_p2;
  wire [3:0] game_logic_1_a0, game_logic_1_a1, game_logic_1_b0, game_logic_1_b1, game_logic_1_c0,
       game_logic_1_c1, game_logic_1_d0, game_logic_1_d1, rgb_video_1_p4, rgb_video_1_p5;
  wire [6:0] game_logic_1_f0_2, game_logic_1_f0_3, game_logic_1_f0_4, game_logic_1_s0_2, game_logic_1_s0_3,
       game_logic_1_s0_4, game_logic_1_s1_2, game_logic_1_s1_3, game_logic_1_s1_4, game_logic_1_s2,
       game_logic_1_s2_2, game_logic_1_s2_3, game_logic_1_s3, game_logic_1_s3_2, game_logic_1_s3_3,
       game_logic_1_s3_4, game_logic_1_s3_5, game_logic_1_s4, game_logic_1_s4_2, game_logic_1_s4_3,
       game_logic_1_s4_4, game_logic_1_s4_5, keyboard_1_data, keyboard_2_data, keyboard_3_data,
       keyboard_4_data, keyboard_5_data, keyboard_6_data, keyboard_7_data, keyboard_8_data, keyboard_9_data,
       keyboard_10_data, keyboard_11_data, keyboard_12_data, keyboard_13_data, keyboard_14_data,
       keyboard_15_data;
  wire [13:0] game_logic_1_f0, game_logic_1_s0, game_logic_1_s1;
  wire [23:0] rgb_video_1_p6;
  wire [34:0] keyboard_16_data;
  wire [34:21] game_logic_1_s2_4;

  Keyboard #(.buflen(1)) keyboard_1 (.clr(button_2_out), .data(keyboard_1_data));  // open: clk, re, avail
  Keyboard #(.buflen(1)) keyboard_2 (.clr(button_2_out), .data(keyboard_2_data));  // open: clk, re, avail
  Keyboard #(.buflen(1)) keyboard_3 (.clr(button_2_out), .data(keyboard_3_data));  // open: clk, re, avail
  Keyboard #(.buflen(1)) keyboard_4 (.clr(button_2_out), .data(keyboard_4_data));  // open: clk, re, avail
  Keyboard #(.buflen(1)) keyboard_5 (.clr(button_2_out), .data(keyboard_5_data));  // open: clk, re, avail
  Button button_1 (.out(button_1_out));
  Button button_2 (.out(button_2_out));
  // RGB_Video #(.cursor("No Cursor"), .height(16), .reset("Synchronous"), .scale(8), .width(16)) rgb_video_1: pin names not known; wires that end beside it: rgb_video_1_p1, rgb_video_1_p2, 1'b1, rgb_video_1_p4, rgb_video_1_p5, rgb_video_1_p6
  Button button_3 (.out(rgb_video_1_p1));
  Clock clock_1 (.out(rgb_video_1_p2));
  Joystick joystick_1 (.x(rgb_video_1_p4), .y(rgb_video_1_p5));
  Hex_Digit_Display hex_digit_display_1 (.value(game_logic_1_a1));  // open: dp
  Hex_Digit_Display hex_digit_display_2 (.value(game_logic_1_a0));  // open: dp
  DotMatrix #(.matrixcols(37)) dotmatrix_1 (
    .col0({7{1'b0}}), .col1(7'b0111110), .col2(7'b0101000), .col3(7'b0101000), .col4(7'b0101000),
    .col5(7'b0111110), .col6({7{1'b0}}), .col7(7'b0111110), .col8(7'b0010000), .col9(7'b0001000),
    .col10(7'b0000100), .col11(7'b0111110), .col12({7{1'b0}}), .col13(7'b0111010), .col14(7'b0101010),
    .col15(7'b0101010), .col16(7'b0101110), .col17({7{1'b0}}), .col18(7'b0111000), .col19(7'b0000110),
    .col20(7'b0011000), .col21(7'b0000110), .col22(7'b0111000), .col23({7{1'b0}}), .col24(7'b0111110),
    .col25(7'b0101010), .col26(7'b0101010), .col27(7'b0101010), .col28({7{1'b0}}), .col29(7'b0111110),
    .col30(7'b0101000), .col31(7'b0101000), .col32(7'b0101000), .col33(7'b0010110), .col34({7{1'b0}}),
    .col35(7'b0100010), .col36({7{1'b0}}));
  Keyboard #(.buflen(1)) keyboard_6 (.clr(button_4_out), .data(keyboard_6_data));  // open: clk, re, avail
  Keyboard #(.buflen(1)) keyboard_7 (.clr(button_4_out), .data(keyboard_7_data));  // open: clk, re, avail
  Keyboard #(.buflen(1)) keyboard_8 (.clr(button_4_out), .data(keyboard_8_data));  // open: clk, re, avail
  Keyboard #(.buflen(1)) keyboard_9 (.clr(button_4_out), .data(keyboard_9_data));  // open: clk, re, avail
  Keyboard #(.buflen(1)) keyboard_10 (.clr(button_4_out), .data(keyboard_10_data));  // open: clk, re, avail
  LED led_1 (.in(game_logic_1_turna));
  DotMatrix #(.matrixcols(39)) dotmatrix_2 (
    .col0({7{1'b0}}), .col1(game_logic_1_f0_4), .col2(game_logic_1_f0_3), .col3(game_logic_1_f0_2),
    .col4(game_logic_1_f0[13:7]), .col5(game_logic_1_f0[6:0]), .col6({7{1'b0}}), .col7(7'b0110000),
    .col8({7{1'b0}}), .col9(7'b0111010), .col10(7'b0101010), .col11(7'b0101010), .col12(7'b0101110),
    .col13({7{1'b0}}), .col14({7{1'b0}}), .col15(7'b0100000), .col16(7'b0100000), .col17(7'b0111110),
    .col18(7'b0100000), .col19(7'b0100000), .col20({7{1'b0}}), .col21(7'b0111100), .col22(7'b0000010),
    .col23(7'b0000010), .col24(7'b0000010), .col25(7'b0111100), .col26({7{1'b0}}), .col27(7'b0111110),
    .col28(7'b0101000), .col29(7'b0101000), .col30(7'b0101000), .col31(7'b0010110), .col32({7{1'b0}}),
    .col33(7'b0111110), .col34(7'b0010000), .col35(7'b0001000), .col36(7'b0000100), .col37(7'b0111110),
    .col38({7{1'b0}}));
  Slider slider_1 (.out(rgb_video_1_p6[7:0]));
  Slider slider_2 (.out(rgb_video_1_p6[15:8]));
  Slider slider_3 (.out(rgb_video_1_p6[23:16]));
  Button button_4 (.out(button_4_out));
  Hex_Digit_Display hex_digit_display_3 (.value(game_logic_1_b1));  // open: dp
  Hex_Digit_Display hex_digit_display_4 (.value(game_logic_1_b0));  // open: dp
  LED led_2 (.in(game_logic_1_turnb));
  DotMatrix #(.matrixcols(31)) dotmatrix_3 (
    .col0({7{1'b0}}), .col1(game_logic_1_s0_4), .col2(game_logic_1_s0_3), .col3(game_logic_1_s0_2),
    .col4(game_logic_1_s0[13:7]), .col5(game_logic_1_s0[6:0]), .col6({7{1'b0}}), .col7(game_logic_1_s1_4),
    .col8(game_logic_1_s1_3), .col9(game_logic_1_s1_2), .col10(game_logic_1_s1[13:7]),
    .col11(game_logic_1_s1[6:0]), .col12({7{1'b0}}), .col13(game_logic_1_s2_4[34:28]),
    .col14(game_logic_1_s2_4[27:21]), .col15(game_logic_1_s2_3), .col16(game_logic_1_s2_2),
    .col17(game_logic_1_s2), .col18({7{1'b0}}), .col19(game_logic_1_s3_5), .col20(game_logic_1_s3_4),
    .col21(game_logic_1_s3_3), .col22(game_logic_1_s3_2), .col23(game_logic_1_s3), .col24({7{1'b0}}),
    .col25(game_logic_1_s4_5), .col26(game_logic_1_s4_4), .col27(game_logic_1_s4_3),
    .col28(game_logic_1_s4_2), .col29(game_logic_1_s4), .col30({7{1'b0}}));
  Keyboard #(.buflen(1)) keyboard_11 (.clr(button_5_out), .data(keyboard_11_data));  // open: clk, re, avail
  Keyboard #(.buflen(1)) keyboard_12 (.clr(button_5_out), .data(keyboard_12_data));  // open: clk, re, avail
  Keyboard #(.buflen(1)) keyboard_13 (.clr(button_5_out), .data(keyboard_13_data));  // open: clk, re, avail
  Keyboard #(.buflen(1)) keyboard_14 (.clr(button_5_out), .data(keyboard_14_data));  // open: clk, re, avail
  Keyboard #(.buflen(1)) keyboard_15 (.clr(button_5_out), .data(keyboard_15_data));  // open: clk, re, avail
  Button button_5 (.out(button_5_out));
  Hex_Digit_Display hex_digit_display_5 (.value(game_logic_1_c1));  // open: dp
  LED led_3 (.in(game_logic_1_turnc));
  Hex_Digit_Display hex_digit_display_6 (.value(game_logic_1_c0));  // open: dp
  Keyboard #(.buflen(1)) keyboard_16 (.clr(button_6_out), .data(keyboard_16_data[6:0]));  // open: clk, re, avail
  Keyboard #(.buflen(1)) keyboard_17 (.clr(button_6_out), .data(keyboard_16_data[13:7]));  // open: clk, re, avail
  Keyboard #(.buflen(1)) keyboard_18 (.clr(button_6_out), .data(keyboard_16_data[20:14]));  // open: clk, re, avail
  Keyboard #(.buflen(1)) keyboard_19 (.clr(button_6_out), .data(keyboard_16_data[27:21]));  // open: clk, re, avail
  Keyboard #(.buflen(1)) keyboard_20 (.clr(button_6_out), .data(keyboard_16_data[34:28]));  // open: clk, re, avail
  Button button_6 (.out(button_6_out));
  Hex_Digit_Display hex_digit_display_7 (.value(game_logic_1_d1));  // open: dp
  LED led_4 (.in(game_logic_1_turnd));
  Hex_Digit_Display hex_digit_display_8 (.value(game_logic_1_d0));  // open: dp
  game_logic game_logic_1 (
    .Reset(button_1_out), .SaveA(Save),
    .A({keyboard_5_data, keyboard_4_data, keyboard_3_data, keyboard_2_data, keyboard_1_data}),
    .SaveB(Save_2),
    .B({keyboard_10_data, keyboard_9_data, keyboard_8_data, keyboard_7_data, keyboard_6_data}),
    .SaveC(Save_3),
    .C({keyboard_15_data, keyboard_14_data, keyboard_13_data, keyboard_12_data, keyboard_11_data}),
    .SaveD(Save_4), .D(keyboard_16_data),
    .f0({game_logic_1_f0_4, game_logic_1_f0_3, game_logic_1_f0_2, game_logic_1_f0}), .A1(game_logic_1_a1),
    .A0(game_logic_1_a0), .B1(game_logic_1_b1), .B0(game_logic_1_b0), .C1(game_logic_1_c1),
    .C0(game_logic_1_c0), .D1(game_logic_1_d1), .D0(game_logic_1_d0), .TurnD(game_logic_1_turnd),
    .TurnC(game_logic_1_turnc), .TurnB(game_logic_1_turnb), .TurnA(game_logic_1_turna),
    .S0({game_logic_1_s0_4, game_logic_1_s0_3, game_logic_1_s0_2, game_logic_1_s0}),
    .S1({game_logic_1_s1_4, game_logic_1_s1_3, game_logic_1_s1_2, game_logic_1_s1}),
    .S2({game_logic_1_s2_4, game_logic_1_s2_3, game_logic_1_s2_2, game_logic_1_s2}),
    .S3({game_logic_1_s3_5, game_logic_1_s3_4, game_logic_1_s3_3, game_logic_1_s3_2, game_logic_1_s3}),
    .S4({game_logic_1_s4_5, game_logic_1_s4_4, game_logic_1_s4_3, game_logic_1_s4_2, game_logic_1_s4}));

  // Notes on the sheet:
  //   Screen Clear Button
  //   Remove
  //   Player A
  //   Score Reset Button
  //   Select "Simulate" menu,
  //   Joystick
  //   To start the game, go to the "five_register circuit"
  //   Player B
  //   Then set "Enable Auto-Tick" and "Auto-Tick Frequency" to 2048.0kHz.
  //   Choose color
  //   Remove
  //   Please enter the answer to the quiz in all capital letters.
  //   Player C
  //   Remove
  //   Remove
  //   Player D
endmodule

module result (
  input  E,
  input  [39:0] Drawing,
  input  [39:0] First,
  input  [39:0] Second,
  input  [39:0] Third,
  output FS,
  output SS,
  output DS,
  output TS
);

  wire five_compator_1_out_3, five_compator_2_out_3, five_compator_3_out_3;

  five_compator five_compator_1 (.in_1(Drawing), .in_2(First), .out_3(five_compator_1_out_3));
  five_compator five_compator_2 (.in_1(Drawing), .in_2(Second), .out_3(five_compator_2_out_3));
  five_compator five_compator_3 (.in_1(Drawing), .in_2(Third), .out_3(five_compator_3_out_3));
  and and_1 (FS, five_compator_1_out_3, E);
  and and_2 (SS, five_compator_2_out_3, E);
  and and_3 (TS, five_compator_3_out_3, E);
  or or_1 (DS, FS, SS, TS);
endmodule

module change_turn (
  input  in_1,
  input  in_2,
  input  in_3,
  input  in_4,
  output out_5,
  output out_6
);

  wire and_1_out, d_ff_1_qn, d_ff_2_qn, nor_1_out, nor_2_out;

  nor nor_1 (nor_1_out, in_1, in_2);
  and and_1 (and_1_out, nor_1_out, nor_2_out);
  nor nor_2 (nor_2_out, in_3, in_4);
  D_Flip_Flop d_ff_1 (.D(d_ff_1_qn), .clk(and_1_out), .Q(out_5), .Qn(d_ff_1_qn));  // open: preset, reset
  D_Flip_Flop d_ff_2 (.D(d_ff_2_qn), .clk(d_ff_1_qn), .Q(out_6), .Qn(d_ff_2_qn));  // open: preset, reset
endmodule

module five_compator (
  input  [39:0] in_1,
  input  [39:0] in_2,
  output out_3
);

  wire and_1_out, and_2_out, and_3_out, comparator_1_eq, comparator_2_eq, comparator_3_eq, comparator_4_eq,
       comparator_5_eq;

  Comparator comparator_1 (.a(in_1[7:0]), .b(in_2[7:0]), .eq(comparator_1_eq));  // open: gt, lt
  Comparator comparator_2 (.a(in_1[15:8]), .b(in_2[15:8]), .eq(comparator_2_eq));  // open: gt, lt
  Comparator comparator_3 (.a(in_1[23:16]), .b(in_2[23:16]), .eq(comparator_3_eq));  // open: gt, lt
  Comparator comparator_4 (.a(in_1[31:24]), .b(in_2[31:24]), .eq(comparator_4_eq));  // open: gt, lt
  Comparator comparator_5 (.a(in_1[39:32]), .b(in_2[39:32]), .eq(comparator_5_eq));  // open: gt, lt
  and and_1 (and_1_out, comparator_1_eq, comparator_2_eq);
  and and_2 (and_2_out, comparator_3_eq, comparator_4_eq);
  and and_3 (and_3_out, and_1_out, and_2_out);
  and and_4 (out_3, and_3_out, comparator_5_eq);
endmodule

module five_register (
  input  Save,
  input  [34:0] in_2,
  output [39:0] out_3
);

  wire clock_1_out, not_1_out;
  wire [7:0] bit_extender_1_out, bit_extender_2_out, bit_extender_3_out, bit_extender_4_out,
       bit_extender_5_out;

  assign bit_extender_1_out = {{1{1'b0}}, in_2[6:0]};  // Bit_Extender bit_extender_1
  not not_1 (not_1_out, Save);
  Clock clock_1 (.out(clock_1_out));
  assign bit_extender_2_out = {{1{1'b0}}, in_2[13:7]};  // Bit_Extender bit_extender_2
  assign bit_extender_3_out = {{1{1'b0}}, in_2[20:14]};  // Bit_Extender bit_extender_3
  assign bit_extender_4_out = {{1{1'b0}}, in_2[27:21]};  // Bit_Extender bit_extender_4
  assign bit_extender_5_out = {{1{1'b0}}, in_2[34:28]};  // Bit_Extender bit_extender_5
  Register register_1 (.D(bit_extender_1_out), .en(not_1_out), .clk(clock_1_out), .Q(out_3[7:0]));  // open: clr
  Register register_2 (.D(bit_extender_2_out), .en(not_1_out), .clk(clock_1_out), .Q(out_3[15:8]));  // open: clr
  Register register_3 (.D(bit_extender_3_out), .en(not_1_out), .clk(clock_1_out), .Q(out_3[23:16]));  // open: clr
  Register register_4 (.D(bit_extender_4_out), .en(not_1_out), .clk(clock_1_out), .Q(out_3[31:24]));  // open: clr
  Register register_5 (.D(bit_extender_5_out), .en(not_1_out), .clk(clock_1_out), .Q(out_3[39:32]));  // open: clr
endmodule

module display_turn (
  input  [1:0] in_1,
  output [34:0] out_2
);

  DotMatrix #(.matrixcols(7)) dotmatrix_1 (
    .col0({7{1'b0}}), .col1(7'b0111110), .col2(7'b0101000), .col3(7'b0101000), .col4(7'b0101000),
    .col5(7'b0111110), .col6({7{1'b0}}));
  DotMatrix #(.matrixcols(7)) dotmatrix_2 (
    .col0({7{1'b0}}), .col1(7'b0111110), .col2(7'b0101010), .col3(7'b0101010), .col4(7'b0101010),
    .col5(7'b0010100), .col6({7{1'b0}}));
  DotMatrix #(.matrixcols(7)) dotmatrix_3 (
    .col0({7{1'b0}}), .col1(7'b0111110), .col2(7'b0100010), .col3(7'b0100010), .col4(7'b0100010),
    .col5(7'b0100010), .col6({7{1'b0}}));
  DotMatrix #(.matrixcols(7)) dotmatrix_4 (
    .col0({7{1'b0}}), .col1(7'b0111110), .col2(7'b0100010), .col3(7'b0100010), .col4(7'b0100010),
    .col5(7'b0011100), .col6({7{1'b0}}));
  Multiplexer #(.select(2), .width(35)) multiplexer_1 (
    .in0(35'h3e50a143e), .in1(35'h3e54a9514), .in2(35'h3e4489122), .in3(35'h3e448911c), .out(out_2),
    .sel(in_1));
endmodule

module game_logic (
  input  Reset,
  input  SaveA,
  input  [34:0] A,
  input  SaveB,
  input  [34:0] B,
  input  SaveC,
  input  [34:0] C,
  input  SaveD,
  input  [34:0] D,
  output [34:0] f0,
  output [3:0] A1,
  output [3:0] A0,
  output [3:0] B1,
  output [3:0] B0,
  output [3:0] C1,
  output [3:0] C0,
  output [3:0] D1,
  output [3:0] D0,
  output TurnD,
  output TurnC,
  output TurnB,
  output TurnA,
  output [34:0] S0,
  output [34:0] S1,
  output [34:0] S2,
  output [34:0] S3,
  output [34:0] S4
);

  wire and_1_out, and_2_out, and_3_out, and_4_out, and_5_out, and_6_out, not_1_out, not_2_out, not_3_out,
       not_4_out, or_1_out, or_2_out, or_3_out, or_4_out, result_1_ds, result_1_fs, result_1_ss, result_1_ts,
       result_2_ds, result_2_fs, result_2_ss, result_2_ts, result_3_ds, result_3_fs, result_3_ss,
       result_3_ts, result_4_ds, result_4_fs, result_4_ss, result_4_ts;
  wire [1:0] change_turn_1_out_5;
  wire [4:0] bit_extender_1_out, bit_extender_2_out, bit_extender_3_out, bit_extender_4_out,
       bit_extender_5_out;
  wire [7:0] subtractor_1_out, subtractor_2_out, subtractor_3_out, subtractor_4_out, subtractor_5_out;
  wire [34:0] display_answer_1_out_2, display_answer_2_out_2, display_answer_3_out_2, display_answer_4_out_2,
       display_answer_5_out_2;
  wire [39:0] five_register_1_out_3, five_register_2_out_3, five_register_3_out_3, five_register_4_out_3,
       multiplexer_1_out;

  Clock clock_1 ();  // open: out
  five_register five_register_1 (.Save(SaveA), .in_2(A), .out_3(five_register_1_out_3));
  five_register five_register_2 (.Save(SaveB), .in_2(B), .out_3(five_register_2_out_3));
  five_register five_register_3 (.Save(SaveC), .in_2(C), .out_3(five_register_3_out_3));
  five_register five_register_4 (.Save(SaveD), .in_2(D), .out_3(five_register_4_out_3));
  and and_1 (and_1_out, SaveA, SaveB, SaveC, SaveD);
  and and_2 (and_2_out, SaveA, SaveB, SaveC, SaveD);
  change_turn change_turn_1 (
    .in_1(SaveA), .in_2(SaveB), .in_3(SaveC), .in_4(SaveD), .out_5(change_turn_1_out_5[0]),
    .out_6(change_turn_1_out_5[1]));
  // PlaRom #(.Contents("1*3 2 2 1 2 2 1 0*4 1 0*4 1 0*4 1")) plarom_1: pin names not known; wires that end beside it: change_turn_1_out_5, {TurnA, TurnB, TurnC, TurnD}
  Multiplexer #(.select(2), .width(40)) multiplexer_1 (
    .in0(five_register_1_out_3), .in1(five_register_2_out_3), .in2(five_register_3_out_3),
    .in3(five_register_4_out_3), .out(multiplexer_1_out), .sel(change_turn_1_out_5));
  Bit_Extender #(.out_width(5), .\type ("zero")) bit_extender_1 (.in(subtractor_1_out), .out(bit_extender_1_out));
  Subtractor subtractor_1 (.a(multiplexer_1_out[7:0]), .b(8'h41), .out(subtractor_1_out));  // open: bin, bout
  Bit_Extender #(.out_width(5), .\type ("zero")) bit_extender_2 (.in(subtractor_2_out), .out(bit_extender_2_out));
  Subtractor subtractor_2 (.a(multiplexer_1_out[15:8]), .b(8'h41), .out(subtractor_2_out));  // open: bin, bout
  Bit_Extender #(.out_width(5), .\type ("zero")) bit_extender_3 (.in(subtractor_3_out), .out(bit_extender_3_out));
  Subtractor subtractor_3 (.a(multiplexer_1_out[23:16]), .b(8'h41), .out(subtractor_3_out));  // open: bin, bout
  Bit_Extender #(.out_width(5), .\type ("zero")) bit_extender_4 (.in(subtractor_4_out), .out(bit_extender_4_out));
  Subtractor subtractor_4 (.a(multiplexer_1_out[31:24]), .b(8'h41), .out(subtractor_4_out));  // open: bin, bout
  Bit_Extender #(.out_width(5), .\type ("zero")) bit_extender_5 (.in(subtractor_5_out), .out(bit_extender_5_out));
  Subtractor subtractor_5 (.a(multiplexer_1_out[39:32]), .b(8'h41), .out(subtractor_5_out));  // open: bin, bout
  display_turn display_turn_1 (.in_1(change_turn_1_out_5), .out_2(f0));
  and and_3 (and_3_out, TurnA, and_1_out);
  and and_4 (and_4_out, TurnB, and_1_out);
  and and_5 (and_5_out, TurnC, and_1_out);
  and and_6 (and_6_out, TurnD, and_1_out);
  display_answer display_answer_1 (.in_1(bit_extender_1_out), .out_2(display_answer_1_out_2));
  display_answer display_answer_2 (.in_1(bit_extender_2_out), .out_2(display_answer_2_out_2));
  display_answer display_answer_3 (.in_1(bit_extender_3_out), .out_2(display_answer_3_out_2));
  display_answer display_answer_4 (.in_1(bit_extender_4_out), .out_2(display_answer_4_out_2));
  display_answer display_answer_5 (.in_1(bit_extender_5_out), .out_2(display_answer_5_out_2));
  Multiplexer #(.width(35)) multiplexer_2 (.in0({35{1'b0}}), .in1(display_answer_1_out_2), .out(S0), .sel(and_2_out));
  Multiplexer #(.width(35)) multiplexer_3 (.in0({35{1'b0}}), .in1(display_answer_2_out_2), .out(S1), .sel(and_2_out));
  Multiplexer #(.width(35)) multiplexer_4 (.in0({35{1'b0}}), .in1(display_answer_3_out_2), .out(S2), .sel(and_2_out));
  Multiplexer #(.width(35)) multiplexer_5 (.in0({35{1'b0}}), .in1(display_answer_4_out_2), .out(S3), .sel(and_2_out));
  Multiplexer #(.width(35)) multiplexer_6 (.in0({35{1'b0}}), .in1(display_answer_5_out_2), .out(S4), .sel(and_2_out));
  result result_1 (
    .E(and_3_out), .Drawing(five_register_1_out_3), .First(five_register_2_out_3),
    .Second(five_register_3_out_3), .Third(five_register_4_out_3), .FS(result_1_fs), .SS(result_1_ss),
    .DS(result_1_ds), .TS(result_1_ts));
  result result_2 (
    .E(and_4_out), .Drawing(five_register_2_out_3), .First(five_register_1_out_3),
    .Second(five_register_3_out_3), .Third(five_register_4_out_3), .FS(result_2_fs), .SS(result_2_ss),
    .DS(result_2_ds), .TS(result_2_ts));
  result result_3 (
    .E(and_5_out), .Drawing(five_register_3_out_3), .First(five_register_1_out_3),
    .Second(five_register_2_out_3), .Third(five_register_4_out_3), .FS(result_3_fs), .SS(result_3_ss),
    .DS(result_3_ds), .TS(result_3_ts));
  result result_4 (
    .E(and_6_out), .Drawing(five_register_4_out_3), .First(five_register_1_out_3),
    .Second(five_register_2_out_3), .Third(five_register_3_out_3), .FS(result_4_fs), .SS(result_4_ss),
    .DS(result_4_ds), .TS(result_4_ts));
  or or_1 (or_1_out, result_1_ds, result_2_fs, result_3_fs, result_4_fs);
  not not_1 (not_1_out, or_1_out);
  or or_2 (or_2_out, result_1_fs, result_2_ds, result_3_ss, result_4_ss);
  not not_2 (not_2_out, or_2_out);
  or or_3 (or_3_out, result_1_ss, result_2_ss, result_3_ds, result_4_ts);
  not not_3 (not_3_out, or_3_out);
  or or_4 (or_4_out, result_1_ts, result_2_ts, result_3_ts, result_4_ds);
  not not_4 (not_4_out, or_4_out);
  decimal_conter_2_digit decimal_conter_2_digit_1 (.Reset(Reset), .CLK(not_1_out), .out_3({A1, A0}));
  decimal_conter_2_digit decimal_conter_2_digit_2 (.Reset(Reset), .CLK(not_2_out), .out_3({B1, B0}));
  decimal_conter_2_digit decimal_conter_2_digit_3 (.Reset(Reset), .CLK(not_3_out), .out_3({C1, C0}));
  decimal_conter_2_digit decimal_conter_2_digit_4 (.Reset(Reset), .CLK(not_4_out), .out_3({D1, D0}));
endmodule

module display_answer (
  input  [4:0] in_1,
  output [34:0] out_2
);

  DotMatrix dotmatrix_1 (
    .col0(out_2[34:28]), .col1(out_2[27:21]), .col2(out_2[20:14]), .col3(out_2[13:7]), .col4(out_2[6:0]));
  Multiplexer #(.select(5), .width(35)) multiplexer_1 (
    .in0(35'h3e50a143e), .in1(35'h3e54a9514), .in2(35'h3e4489122), .in3(35'h3e448911c), .in4(35'h3e54a952a),
    .in5(35'h3e50a1428), .in6(35'h3e44a952e), .in7(35'h3e102043e), .in8(35'h2244f9122), .in9(35'h2244f9020),
    .in10(35'h3e1020a22), .in11(35'h3e0408102), .in12(35'h3e202083e), .in13(35'h3e202023e),
    .in14(35'h1c448911c), .in15(35'h3e50a1410), .in16(35'h1050a143e), .in17(35'h3e50a1416),
    .in18(35'h3a54a952e), .in19(35'h2040f9020), .in20(35'h3c040813c), .in21(35'h380808238),
    .in22(35'h380c60338), .in23(35'h222820a22), .in24(35'h202038820), .in25(35'h224ca9922),
    .in26({35{1'b0}}), .in27({35{1'b0}}), .in28({35{1'b0}}), .in29({35{1'b0}}), .in30({35{1'b0}}),
    .in31({35{1'b0}}), .out(out_2), .sel(in_1));

  // Notes on the sheet:
  //   A
  //   B
  //   C
  //   D
  //   E
  //   F
  //   G
  //   H
  //   I
  //   J
  //   K
  //   L
  //   M
  //   N
  //   O
  //   P
  //   Q
  //   R
  //   S
  //   T
  //   U
  //   V
  //   W
  //   X
  //   Y
  //   Z
  //   NONE
endmodule

module BCD_conter (
  input  Reset,
  input  CLK,
  output Qa,
  output Qb,
  output Qc,
  output Qd
);

  wire and_1_out, not_1_out, not_2_out, not_3_out, not_4_out, not_5_out, not_6_out, not_7_out, not_8_out,
       not_9_out, or_1_out;

  J_K_Flip_Flop j_k_ff_1 (.J(1'b1), .K(1'b1), .clk(not_1_out), .Q(Qa), .preset(1'b0), .reset(not_2_out));  // open: Qn
  not not_1 (not_1_out, CLK);
  not not_2 (not_2_out, not_9_out);
  J_K_Flip_Flop j_k_ff_2 (.J(1'b1), .K(1'b1), .clk(not_3_out), .Q(Qb), .preset(1'b0), .reset(not_4_out));  // open: Qn
  not not_3 (not_3_out, Qa);
  not not_4 (not_4_out, not_9_out);
  J_K_Flip_Flop j_k_ff_3 (.J(1'b1), .K(1'b1), .clk(not_5_out), .Q(Qc), .preset(1'b0), .reset(not_6_out));  // open: Qn
  not not_5 (not_5_out, Qb);
  not not_6 (not_6_out, not_9_out);
  J_K_Flip_Flop j_k_ff_4 (.J(1'b1), .K(1'b1), .clk(not_7_out), .Q(Qd), .preset(1'b0), .reset(not_8_out));  // open: Qn
  not not_7 (not_7_out, Qc);
  not not_8 (not_8_out, not_9_out);
  and and_1 (and_1_out, Qb, Qd);
  or or_1 (or_1_out, and_1_out, Reset);
  not not_9 (not_9_out, or_1_out);
endmodule

module decimal_conter_2_digit (
  input  Reset,
  input  CLK,
  output [7:0] out_3
);

  BCD_conter bcd_conter_1 (.Reset(Reset), .CLK(CLK), .Qa(out_3[0]), .Qb(out_3[1]), .Qc(out_3[2]), .Qd(out_3[3]));
  BCD_conter bcd_conter_2 (.Reset(Reset), .CLK(out_3[3]), .Qa(out_3[4]), .Qb(out_3[5]), .Qc(out_3[6]), .Qd(out_3[7]));
endmodule
